# Fritzing sketch sensors-client-scheme_D1_mini (saved by Fritzing 0.9.3b)
breadboards: 1

parts:
  Part1 = BME280 Breakout
  R1 = PHOTOCELL [package=photocell-kit]
  R2 = Resistor [tolerance=±5% resistance=10k package="2010 [SMD]"]
  WeMos_D1_Mini1 = WeMos D1 Mini

nets:
  N1: Part1.SDI/SDA, WeMos_D1_Mini1.D2
  N2: Part1.SCK/SCL, WeMos_D1_Mini1.D1
  N3: R1.P$1, WeMos_D1_Mini1.3V3
  N4: R1.P$2, R2.Pin_0, WeMos_D1_Mini1.A0

custom parts:
  WeMos D1 Mini: The D1 mini is a mini wifi board based on ESP-8266EX.
